// Logisim project FSM.circ as structural Verilog: 2 circuits, main circuit main
// 01101
module main (
  input  W
);

  wire _4511_a_2, _4511_b_2, _4511_c_2, _4511_d_2, _4511_e, _4511_f, _4511_g, Clear_out, Clk_out, FSM_q0,
       FSM_q1, FSM_q2, FSM_y;

  Button Clear (.out(Clear_out));
  LED y (.in(FSM_y));
  Clock Clk (.out(Clk_out));
  FSM_10110 FSM (.W(W), .Clock(Clk_out), .Clear(Clear_out), .Y(FSM_y), .Q2(FSM_q2), .Q1(FSM_q1), .Q0(FSM_q0));
  _4511 _4511 (
    .D(1'b0), .C(FSM_q2), .B(FSM_q1), .A(FSM_q0), .A_2(_4511_a_2), .B_2(_4511_b_2), .C_2(_4511_c_2),
    .D_2(_4511_d_2), .E(_4511_e), .F(_4511_f), .G(_4511_g));
  _7_Segment_Display u_7_segment_display_1 (
    .g(_4511_g), .f(_4511_f), .a(_4511_a_2), .b(_4511_b_2), .e(_4511_e), .d(_4511_d_2), .c(_4511_c_2));  // open: dp
endmodule

module FSM_10110 (
  input  W,
  input  Clock,
  input  Clear,
  output Y,
  output Q2,
  output Q1,
  output Q0
);

  wire and_1_out, and_2_out, and_3_out, and_4_out, and_5_out, and_6_out, and_7_out, not_1_out, or_1_out,
       or_2_out, or_3_out, or_4_out, or_5_out, or_6_out, or_7_out, Q1_qn, Q2_qn;

  not not_1 (not_1_out, W);
  or or_1 (or_1_out, Q0, Q1);
  or or_2 (or_2_out, or_1_out, not_1_out);
  and and_1 (and_1_out, not_1_out, Q1);
  and and_2 (and_2_out, and_1_out, Q0);
  J_K_Flip_Flop u_Q2 (
    .J(and_2_out), .clk(Clock), .K(or_2_out), .Q(Q2), .Qn(Q2_qn), .preset(1'b0), .en(1'b1), .reset(Clear));
  or or_3 (or_3_out, Q0, Q2);
  or or_4 (or_4_out, or_3_out, not_1_out);
  and and_3 (and_3_out, W, Q0);
  J_K_Flip_Flop u_Q1 (
    .J(and_3_out), .clk(Clock), .K(or_4_out), .Q(Q1), .Qn(Q1_qn), .preset(1'b0), .en(1'b1), .reset(Clear));
  and and_4 (and_4_out, Q2_qn, W);
  or or_5 (or_5_out, Q1, and_4_out);
  and and_5 (and_5_out, not_1_out, Q1_qn);
  and and_6 (and_6_out, Q2, Q1_qn);
  or or_6 (or_6_out, and_5_out, and_6_out);
  or or_7 (or_7_out, or_6_out, and_7_out);
  and and_7 (and_7_out, Q2_qn, Q1);
  J_K_Flip_Flop u_Q0 (
    .J(or_7_out), .clk(Clock), .K(or_5_out), .Q(Q0), .preset(1'b0), .en(1'b1), .reset(Clear));  // open: Qn
  and and_8 (Y, and_6_out, Q0);
endmodule
