// Logisim project senha 3 a 9.circ as structural Verilog
module senha (
  input  A,
  input  B,
  input  C,
  input  D,
  output S
);

  wire and_1_out, and_2_out, and_3_out, not_1_out, not_2_out, not_3_out, not_4_out;

  not not_1 (not_1_out, A);
  and and_1 (and_1_out, not_1_out, C, D);
  not not_2 (not_2_out, A);
  and and_2 (and_2_out, not_2_out, B);
  and and_3 (and_3_out, A, not_3_out, not_4_out);
  not not_3 (not_3_out, B);
  not not_4 (not_4_out, C);
  or or_1 (S, and_1_out, and_2_out, and_3_out);
endmodule
